// Logisim project CpuAlejandro.circ as structural Verilog: 5 circuits, main circuit CPU 
module ALU (
  input  [15:0] Input_A,
  input  [15:0] Input_B,
  input  [2:0] ALU_Op,
  output [15:0] Output,
  output Zero
);

  wire [15:0] adder_1_out, adder_2_out, and_1_out, not_1_out, or_1_out, subtractor_1_out;

  assign and_1_out = Input_A & Input_B;  // AND_Gate and_1, 16 bits wide
  assign or_1_out = Input_A | Input_B;  // OR_Gate or_1, 16 bits wide
  assign not_1_out = ~Input_A;  // NOT_Gate not_1, 16 bits wide
  Adder #(.width(16)) adder_1 (.a(Input_A), .b(Input_B), .out(adder_1_out));  // open: cin, cout
  Subtractor #(.width(16)) subtractor_1 (.a(Input_A), .b(Input_B), .out(subtractor_1_out));  // open: bin, bout
  Adder #(.width(16)) adder_2 (.a(Input_A), .b({16{1'b0}}), .out(adder_2_out));  // open: cin, cout
  Multiplexer #(.select(3), .width(16), .enable("false")) multiplexer_1 (
    .in0(and_1_out), .in1(or_1_out), .in2(not_1_out), .in3(adder_1_out), .in4(subtractor_1_out),
    .in5(adder_2_out), .out(Output), .sel(ALU_Op));  // open: in6, in7
  nor nor_1 (Zero, Output[0], Output[1], Output[2], Output[3], Output[4], Output[5], Output[6], Output[7], Output[8], Output[9], Output[10], Output[11], Output[12], Output[13], Output[14], Output[15]);

  // Notes on the sheet:
  //   AluOp
  //   000: AND
  //   001: Or
  //   010: Not
  //   011: Sum
  //   100: Sub
  //   101: Zero?
endmodule

// RF
module Register_File (
  input  [3:0] rs,
  input  [3:0] rt,
  input  [3:0] rd,
  input  [15:0] Write_Data,
  input  Clock,
  input  Reg_Write,
  output [15:0] rs_2,
  output [15:0] rt_2,
  output [15:0] rd_2
);

  wire and_1_out, and_2_out, and_3_out, and_4_out, and_5_out, and_6_out, and_7_out, and_8_out, and_9_out,
       and_10_out, and_11_out, and_12_out, and_13_out, and_14_out, and_15_out, and_16_out, and_17_out,
       demultiplexer_1_out0, demultiplexer_1_out1, demultiplexer_1_out2, demultiplexer_1_out3,
       demultiplexer_1_out4, demultiplexer_1_out5, demultiplexer_1_out6, demultiplexer_1_out7,
       demultiplexer_1_out8, demultiplexer_1_out9, demultiplexer_1_out10, demultiplexer_1_out11,
       demultiplexer_1_out12, demultiplexer_1_out13, demultiplexer_1_out14, demultiplexer_1_out15;
  wire [15:0] register_1_q, register_2_q, register_3_q, register_4_q, register_5_q, register_6_q,
       register_7_q, register_8_q, register_9_q, register_10_q, register_11_q, register_12_q, register_13_q,
       register_14_q, register_15_q, register_16_q;

  Demultiplexer #(.select(4), .enable("false")) demultiplexer_1 (
    .out0(demultiplexer_1_out0), .out1(demultiplexer_1_out1), .out2(demultiplexer_1_out2),
    .out3(demultiplexer_1_out3), .out4(demultiplexer_1_out4), .out5(demultiplexer_1_out5),
    .out6(demultiplexer_1_out6), .out7(demultiplexer_1_out7), .out8(demultiplexer_1_out8),
    .out9(demultiplexer_1_out9), .out10(demultiplexer_1_out10), .out11(demultiplexer_1_out11),
    .out12(demultiplexer_1_out12), .out13(demultiplexer_1_out13), .out14(demultiplexer_1_out14),
    .out15(demultiplexer_1_out15), .in(1'b1), .sel(rd));
  and and_1 (and_1_out, Clock, Reg_Write);
  and and_2 (and_2_out, and_1_out, demultiplexer_1_out0);
  and and_3 (and_3_out, and_1_out, demultiplexer_1_out1);
  and and_4 (and_4_out, and_1_out, demultiplexer_1_out2);
  and and_5 (and_5_out, and_1_out, demultiplexer_1_out3);
  and and_6 (and_6_out, and_1_out, demultiplexer_1_out4);
  and and_7 (and_7_out, and_1_out, demultiplexer_1_out5);
  and and_8 (and_8_out, and_1_out, demultiplexer_1_out6);
  and and_9 (and_9_out, and_1_out, demultiplexer_1_out7);
  and and_10 (and_10_out, and_1_out, demultiplexer_1_out8);
  and and_11 (and_11_out, and_1_out, demultiplexer_1_out9);
  and and_12 (and_12_out, and_1_out, demultiplexer_1_out10);
  and and_13 (and_13_out, and_1_out, demultiplexer_1_out11);
  and and_14 (and_14_out, and_1_out, demultiplexer_1_out12);
  and and_15 (and_15_out, and_1_out, demultiplexer_1_out13);
  and and_16 (and_16_out, and_1_out, demultiplexer_1_out14);
  and and_17 (and_17_out, and_1_out, demultiplexer_1_out15);
  Register #(.width(16)) register_1 (.D(Write_Data), .Q(register_1_q), .clk(and_2_out));  // open: en, clr
  Register #(.width(16)) register_2 (.D(Write_Data), .Q(register_2_q), .clk(and_3_out));  // open: en, clr
  Register #(.width(16)) register_3 (.D(Write_Data), .Q(register_3_q), .clk(and_4_out));  // open: en, clr
  Register #(.width(16)) register_4 (.D(Write_Data), .Q(register_4_q), .clk(and_5_out));  // open: en, clr
  Register #(.width(16)) register_5 (.D(Write_Data), .Q(register_5_q), .clk(and_6_out));  // open: en, clr
  Register #(.width(16)) register_6 (.D(Write_Data), .Q(register_6_q), .clk(and_7_out));  // open: en, clr
  Register #(.width(16)) register_7 (.D(Write_Data), .Q(register_7_q), .clk(and_8_out));  // open: en, clr
  Register #(.width(16)) register_8 (.D(Write_Data), .Q(register_8_q), .clk(and_9_out));  // open: en, clr
  Register #(.width(16)) register_9 (.D(Write_Data), .Q(register_9_q), .clk(and_10_out));  // open: en, clr
  Register #(.width(16)) register_10 (.D(Write_Data), .Q(register_10_q), .clk(and_11_out));  // open: en, clr
  Register #(.width(16)) register_11 (.D(Write_Data), .Q(register_11_q), .clk(and_12_out));  // open: en, clr
  Register #(.width(16)) register_12 (.D(Write_Data), .Q(register_12_q), .clk(and_13_out));  // open: en, clr
  Register #(.width(16)) register_13 (.D(Write_Data), .Q(register_13_q), .clk(and_14_out));  // open: en, clr
  Register #(.width(16)) register_14 (.D(Write_Data), .Q(register_14_q), .clk(and_15_out));  // open: en, clr
  Register #(.width(16)) register_15 (.D(Write_Data), .Q(register_15_q), .clk(and_16_out));  // open: en, clr
  Register #(.width(16)) register_16 (.D(Write_Data), .Q(register_16_q), .clk(and_17_out));  // open: en, clr
  Multiplexer #(.select(4), .width(16), .enable("false")) multiplexer_1 (
    .in0(register_1_q), .in1(register_2_q), .in2(register_3_q), .in3(register_4_q), .in4(register_5_q),
    .in5(register_6_q), .in6(register_7_q), .in7(register_8_q), .in8(register_9_q), .in9(register_10_q),
    .in10(register_11_q), .in11(register_12_q), .in12(register_13_q), .in13(register_14_q),
    .in14(register_15_q), .in15(register_16_q), .out(rs_2), .sel(rs));
  Multiplexer #(.select(4), .width(16), .enable("false")) multiplexer_2 (
    .in0(register_1_q), .in1(register_2_q), .in2(register_3_q), .in3(register_4_q), .in4(register_5_q),
    .in5(register_6_q), .in6(register_7_q), .in7(register_8_q), .in8(register_9_q), .in9(register_10_q),
    .in10(register_11_q), .in11(register_12_q), .in12(register_13_q), .in13(register_14_q),
    .in14(register_15_q), .in15(register_16_q), .out(rt_2), .sel(rt));
  Multiplexer #(.select(4), .width(16), .enable("false")) multiplexer_3 (
    .in0(register_1_q), .in1(register_2_q), .in2(register_3_q), .in3(register_4_q), .in4(register_5_q),
    .in5(register_6_q), .in6(register_7_q), .in7(register_8_q), .in8(register_9_q), .in9(register_10_q),
    .in10(register_11_q), .in11(register_12_q), .in12(register_13_q), .in13(register_14_q),
    .in14(register_15_q), .in15(register_16_q), .out(rd_2), .sel(rd));
endmodule

module Control (
  input  [3:0] Opcode,
  output Jump,
  output Branch,
  output MemRead,
  output MemtoReg,
  output MemWrite,
  output AluSrc,
  output RegWrite,
  output rs_or_rd,
  output ldhi,
  output [2:0] AluOP
);

  ROM #(.addrWidth(4), .dataWidth(9)) rom_1 (
    .addr(Opcode), .data({ldhi, rs_or_rd, RegWrite, AluSrc, MemWrite, MemtoReg, MemRead, Branch, Jump}));  // open: sel
  ROM #(.addrWidth(4), .dataWidth(3)) rom_2 (.addr(Opcode), .data(AluOP));  // open: sel

  // Notes on the sheet:
  //   contents of rom_1 (hex, n*v repeats v):
  //   40 40 4c 10 40 40 40 0 e0 140 82 82 0 1 1 1
  //   contents of rom_2 (hex, n*v repeats v):
  //   3 4 3 3 0 1 2 0 3 3 4 5
endmodule

module CPU (
);

  wire alu_1_zero, and_1_out, and_2_out, Clock_out, control_1_alusrc, control_1_branch, control_1_jump,
       control_1_ldhi, control_1_memread, control_1_memtoreg, control_1_memwrite, control_1_regwrite,
       control_1_rs_or_rd, not_1_out, or_1_out, Reset_out;
  wire [2:0] control_1_aluop;
  wire [3:0] multiplexer_1_out;
  wire [15:0] adder_1_out, adder_2_out, alu_1_output, bit_extender_1_out, bit_extender_2_out, ldhi_1_out_2,
       multiplexer_2_out, multiplexer_3_out, multiplexer_4_out, multiplexer_5_out, multiplexer_6_out,
       multiplexer_7_out, multiplexer_8_out, multiplexer_9_out, multiplexer_10_out, multiplexer_11_out, PC_q,
       ram_1_data, ram_2_data, register_file_1_rd_2, register_file_1_rs_2, register_file_1_rt_2;

  Clock Clock (.out(Clock_out));
  Register #(.width(16), .trigger("falling")) PC (.D(adder_1_out), .Q(PC_q), .clk(Clock_out));  // open: en, clr
  Adder #(.width(16)) adder_1 (.a(PC_q), .b(multiplexer_11_out), .out(adder_1_out));  // open: cin, cout
  Button Reset (.out(Reset_out));
  RAM #(.addrWidth(16), .dataWidth(16)) ram_1 (.addr(PC_q), .data(ram_1_data), .clr(Reset_out));  // open: sel, clk, ld
  assign bit_extender_1_out = {{8{ram_1_data[7]}}, ram_1_data[7:0]};  // Bit_Extender bit_extender_1
  Control control_1 (
    .Opcode(ram_1_data[15:12]), .Jump(control_1_jump), .Branch(control_1_branch),
    .MemRead(control_1_memread), .MemtoReg(control_1_memtoreg), .MemWrite(control_1_memwrite),
    .AluSrc(control_1_alusrc), .RegWrite(control_1_regwrite), .rs_or_rd(control_1_rs_or_rd),
    .ldhi(control_1_ldhi), .AluOP(control_1_aluop));
  assign bit_extender_2_out = {{4{ram_1_data[7]}}, {ram_1_data[7:0], ram_1_data[11:8]}};  // Bit_Extender bit_extender_2
  Multiplexer #(.width(4), .enable("false")) multiplexer_1 (
    .in0(ram_1_data[11:8]), .in1(4'b0001), .out(multiplexer_1_out), .sel(control_1_jump));
  ldhi ldhi_1 (.in_1(ram_1_data[7:0]), .out_2(ldhi_1_out_2));
  Adder #(.width(16)) adder_2 (.a(PC_q), .b(16'h1), .out(adder_2_out));  // open: cin, cout
  Register_File register_file_1 (
    .rs(ram_1_data[7:4]), .rt(ram_1_data[3:0]), .rd(multiplexer_1_out), .Write_Data(multiplexer_2_out),
    .Clock(Clock_out), .Reg_Write(control_1_regwrite), .rs_2(register_file_1_rs_2),
    .rt_2(register_file_1_rt_2), .rd_2(register_file_1_rd_2));
  Multiplexer #(.width(16), .enable("false")) multiplexer_2 (
    .in0(multiplexer_7_out), .in1(ldhi_1_out_2), .out(multiplexer_2_out), .sel(control_1_ldhi));
  Multiplexer #(.width(16), .enable("false")) multiplexer_3 (
    .in0(bit_extender_2_out), .in1(alu_1_output), .out(multiplexer_3_out), .sel(control_1_jump));
  Multiplexer #(.width(16), .enable("false")) multiplexer_4 (
    .in0(register_file_1_rt_2), .in1(register_file_1_rd_2), .out(multiplexer_4_out), .sel(control_1_rs_or_rd));
  Multiplexer #(.width(16), .enable("false")) multiplexer_5 (
    .in0(register_file_1_rs_2), .in1(bit_extender_1_out), .out(multiplexer_5_out), .sel(control_1_alusrc));
  and and_1 (and_1_out, alu_1_zero, control_1_branch);
  ALU alu_1 (
    .Input_A(multiplexer_4_out), .Input_B(multiplexer_5_out), .ALU_Op(control_1_aluop),
    .Output(alu_1_output), .Zero(alu_1_zero));
  Multiplexer #(.width(16), .enable("false")) multiplexer_6 (
    .in0(alu_1_output), .in1(ram_2_data), .out(multiplexer_6_out), .sel(control_1_memtoreg));
  Multiplexer #(.width(16), .enable("false")) multiplexer_7 (
    .in0(multiplexer_6_out), .in1(adder_2_out), .out(multiplexer_7_out), .sel(control_1_jump));
  Multiplexer #(.width(16), .enable("false")) multiplexer_8 (
    .in0(adder_1_out), .in1(16'h1), .out(multiplexer_8_out), .sel(and_1_out));
  Multiplexer #(.width(16), .enable("false")) multiplexer_9 (
    .in0(multiplexer_8_out), .in1(bit_extender_1_out), .out(multiplexer_9_out), .sel(and_2_out));
  and and_2 (and_2_out, not_1_out, control_1_branch);
  not not_1 (not_1_out, alu_1_zero);
  Multiplexer #(.width(16), .enable("false")) multiplexer_10 (
    .in0(multiplexer_9_out), .in1(multiplexer_3_out), .out(multiplexer_10_out), .sel(control_1_jump));
  or or_1 (or_1_out, control_1_jump, control_1_branch);
  RAM #(.addrWidth(16), .dataWidth(16), .bus("separate")) ram_2 (
    .addr(alu_1_output), .din(register_file_1_rd_2), .data(ram_2_data), .str(control_1_memwrite),
    .clk(Clock_out), .ld(control_1_memread), .clr(Reset_out));  // open: sel
  Multiplexer #(.width(16), .enable("false")) multiplexer_11 (
    .in0(16'h1), .in1(multiplexer_10_out), .out(multiplexer_11_out), .sel(or_1_out));

  // Notes on the sheet:
  //   Alejandro A. Sánchez
  //   804-10-7908
  //   Instruction Memory
  //   jal
  //   16 Bit CPU
  //   rs or rd?
  //   ldhi?
  //   jr?
  //   AluSrc
  //   bz
  //   jal
  //   bnz
  //   MemtoReg
  //   jump
  //   Memory
  //   CCOM 4086: Computer Architecture
endmodule

module ldhi (
  input  [7:0] in_1,
  output [15:0] out_2
);

  wire [15:0] bit_extender_1_out;

  assign bit_extender_1_out = {{8{in_1[7]}}, in_1};  // Bit_Extender bit_extender_1
  Shifter #(.width(16)) shifter_1 (.in(bit_extender_1_out), .\dist (4'b1000), .out(out_2));
endmodule
